# Fritzing sketch mini_serial_console (saved by Fritzing 0.9.3b)
breadboards: 2

parts:
  U1 = 20x4 LCD display [part_number=20x4]
  U2 = Raspberry Pi Pico
  R8 = Resistor [tolerance=±5% resistance=560 package=THT]
  R17 = Resistor [tolerance=±5% resistance=1k package=THT]
  Q3 = NPN-Transistor [part_number=BC109 package="TO92 [THT]"]
  R14 = Resistor [tolerance=±5% resistance=1k package=THT]
  R24 = Resistor [tolerance=±5% resistance=10k package=THT]
  R18 = Resistor [tolerance=±5% resistance=10k package=THT]
  R21 = Resistor [tolerance=±5% resistance=10k package=THT]
  R20 = Resistor [tolerance=±5% resistance=10k package=THT]
  R22 = Resistor [tolerance=±5% resistance=10k package=THT]
  R19 = Resistor [tolerance=±5% resistance=10k package=THT]
  R16 = Resistor [tolerance=±5% resistance=1k package=THT]
  R15 = Resistor [tolerance=±5% resistance=1k package=THT]
  R13 = Resistor [tolerance=±5% resistance=1k package=THT]
  R25 = Resistor [tolerance=±5% resistance=10k package=THT]
  R23 = Resistor [tolerance=±5% resistance=10k package=THT]
  R12 = Resistor [tolerance=±5% resistance=1k package=THT]
  R9 = Resistor [tolerance=±5% resistance=1k package=THT]
  R11 = Resistor [tolerance=±5% resistance=1k package=THT]
  R10 = Resistor [tolerance=±5% resistance=1k package=THT]
  PB2 = Pushbutton [package=THT]
  PB4 = Pushbutton [package=THT]
  PB5 = Pushbutton [package=THT]
  PB3 = Pushbutton [package=THT]
  PB0 = Pushbutton [package=THT]
  PB1 = Pushbutton [package=THT]
  JP3-JP2 = DIP SWITCH [package=dipswitch-02]
  J2 = male pin header, 3 pins [form="♂ (male)"]
  JP1 = male pin header, 2 pins [form="♂ (male)"]
  C2 = Ceramic Capacitor [capacitance=100nF package="100 mil [THT, multilayer]"]
  C4 = Ceramic Capacitor [capacitance=100nF package="100 mil [THT, multilayer]"]
  C5 = Ceramic Capacitor [capacitance=100nF package="100 mil [THT, multilayer]"]
  C1 = Electrolytic Capacitor [capacitance=1000µF package="300 mil [THT, electrolytic]"]
  R6 = Resistor [tolerance=±5% resistance=10k package=THT]
  Q4 = NPN-Transistor [part_number=BC548 package="TO92 [THT]"]
  R4 = Resistor [tolerance=±5% resistance=4.7k package=THT]
  R2 = Resistor [tolerance=±5% resistance=4.7k package=THT]
  D2 = Rectifier Diode [part_number=1N4148 package="300 mil [THT]"]
  R1 = Resistor [tolerance=±5% resistance=4.7k package=THT]
  C3 = Ceramic Capacitor [capacitance=100nF package="100 mil [THT, multilayer]"]
  J3 = male pin header, 3 pins [form="♂ (male)"]
  R5 = Resistor [tolerance=±5% resistance=10k package=THT]
  R3 = Resistor [tolerance=±5% resistance=10k package=THT]
  Q5 = PNP-Transistor [part_number=BC559 package="TO92 [THT]"]
  J1 = male pin header, 2 pins [form="♂ (male)"]
  R7 = Resistor [tolerance=±10% resistance=10k package=THT]

nets:
  N1: U1.Vss, U1.R/W, U2.pin_3, U2.pin_8, U2.pin_13, U2.pin_18, U2.pin_23, U2.pin_28, U2.pin_33, U2.pin_38, Q3.E, PB2.leg1, PB4.leg1, PB5.leg1, PB3.leg1, PB0.leg1, PB1.leg1, JP3-JP2.1, JP3-JP2.2, J2.pin3, JP1.pin1, C2.0, C4.0, C5.0, C1.-, Q4.E, R4.Pin_0, C3.0, J3.pin3, J1.pin2, R7.Pin_0
  N2: U1.Vdd, U1.A_+, U2.pin_40, R24.Pin_1, R18.Pin_0, R21.Pin_1, R20.Pin_1, R22.Pin_0, R19.Pin_0, R25.Pin_1, R23.Pin_0, C2.1, C4.1, C5.1, C1.+, R6.Pin_0, R3.Pin_0, Q5.C, J1.pin1
  N3: U1.Vo, R7.Pin_1
  N4: U1.RS, U2.pin_9
  N5: U1.E, U2.pin_10
  N6: U1.DB0, U2.pin_4
  N7: U1.DB1, U2.pin_5
  N8: U1.DB2, U2.pin_6
  N9: U1.DB3, U2.pin_7
  N10: U1.DB4, U2.pin_14
  N11: U1.DB5, U2.pin_15
  N12: U1.DB6, U2.pin_16
  N13: U1.DB7, U2.pin_17
  N14: U1.K_-, R8.Pin_1
  N15: U2.pin_1, J2.pin1
  N16: U2.pin_2, J2.pin2
  N17: U2.pin_11, R5.Pin_0
  N18: U2.pin_12, R6.Pin_1, Q4.C
  N19: U2.pin_19, R17.Pin_1
  N20: U2.pin_20, R16.Pin_1
  N21: U2.pin_21, R15.Pin_1
  N22: U2.pin_22, R14.Pin_1
  N23: U2.pin_24, R13.Pin_1
  N24: U2.pin_25, R12.Pin_1
  N25: U2.pin_26, R11.Pin_1
  N26: U2.pin_27, R10.Pin_1
  N27: U2.pin_29, R9.Pin_1
  N28: U2.pin_30, JP1.pin2
  N29: R8.Pin_0, Q3.C
  N30: R17.Pin_0, Q3.B
  N31: R14.Pin_0, R23.Pin_1, PB0.leg0
  N32: R24.Pin_0, R15.Pin_0, JP3-JP2.4
  N33: R18.Pin_1, R9.Pin_0, PB5.leg0
  N34: R21.Pin_0, R12.Pin_0, PB2.leg0
  N35: R20.Pin_0, R11.Pin_0, PB3.leg0
  N36: R22.Pin_1, R13.Pin_0, PB1.leg0
  N37: R19.Pin_1, R10.Pin_0, PB4.leg0
  N38: R16.Pin_0, R25.Pin_0, JP3-JP2.3
  N39: Q4.B, R4.Pin_1, R2.Pin_1
  N40: R2.Pin_0, D2.cathode, J3.pin2
  N41: D2.anode, R1.Pin_0, C3.1
  N42: R1.Pin_1, J3.pin1, Q5.E
  N43: R5.Pin_1, R3.Pin_1, Q5.B

notes:
  CONNECTORS JUMPERS
  J1: Power supply JP1: reset
  1: +5V JP2-3: operation modes
  2: GND
  Op. mode JP3 JP2
  J2: TTL serial port ----------------------------
  1: TXD Mode #0 OFF OFF
  1: RXD Mode #1 OFF ON
  1: GND Mode #2 ON OFF
  Mode #3 ON ON
  J3: RS232C serial port
  1: TXD
  2: RXD
  3: GND

custom parts:
  20x4 LCD display: 20x4 character display. CHECK LED POLARITY BEFORE CONNECTING POWER Some versions of the dispaly have the polarity of the LED pins "A" and "K" reversed.
  Raspberry Pi Pico: Raspberry Pi Pico. Based around the RP2040 microcontroller the Pico is a low cost microcontroller device bringing Raspberry Pi quality, cost, and easy of use to the microcontroller space. Jan 2021, Split part in to two versions: tht (this one) and SMD. This one will drill holes for a .1 in header in pcb to allow plugging in the module as well as providing pads to solder the module to the top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
